// Digital circuit SimulacionDigital.dig as structural Verilog
module SimulacionDigital (
  input  IO1,
  input  IO2,
  input  IO3,
  input  IO4,
  output QO2,
  output QO3,
  output QO4,
  output QO1,
  output QO5
);

  wire and_1_out, nor_1_out, not_1_out;

  not not_1 (not_1_out, IO4);
  nor nor_1 (nor_1_out, IO2, IO3);
  or or_1 (QO5, IO3, IO4);
  and and_1 (and_1_out, not_1_out, nor_1_out);
  or or_2 (QO1, IO1, and_1_out);

  assign QO2 = IO2;
  assign QO3 = IO3;
  assign QO4 = IO4;
endmodule
